# Fritzing sketch SchemaCircuito (saved by Fritzing 0.9.3b)
breadboards: 2

parts:
  U1 = LuaNode32 / ESP32 [part_number=ESP32S-PIN30]
  Componente1 = Adafruit VL53L1X [part_number="Adafruit #3967"]
  Componente2 = Adafruit VL53L1X [part_number="Adafruit #3967"]
  GY1 = MPU-6050 Board GY-521 [form="♀ (female)" package=THT]
  A1 = DFR0379
  S1 = H-Bridge with L298N
  DC_Mot_Enc1 = DC Motor with two-phase hall-encoder [part_number=VT-E-G25A-06-177E]
  DC_Mot_Enc2 = DC Motor with two-phase hall-encoder [part_number=VT-E-G25A-06-177E]
  Grove1 = Grove OLED 128x96
  S2 = Square Pushbutton
  BAT1 = 12 battery [package=battery]

nets:
  N1: U1.D34, DC_Mot_Enc2.pin3
  N2: U1.D35, DC_Mot_Enc2.pin4
  N3: U1.D32, DC_Mot_Enc1.pin3
  N4: U1.D33, DC_Mot_Enc1.pin4
  N5: U1.D25, S1.IN4
  N6: U1.D26, S1.IN3
  N7: U1.D27, S1.IN2
  N8: U1.D14, S1.IN1
  N9: U1.D12, S1.ENA
  N10: U1.D13, S1.ENB
  GND: U1.GND, Componente1.GND, Componente2.GND, GY1.pin2, A1.Pin_3, A1.Pin_5, A1.Pin_6, S1.GND, DC_Mot_Enc1.pin2, DC_Mot_Enc2.pin2, Grove1.GND, BAT1.-
  VIN: U1.Vin, A1.Pin_7, S1.5V, DC_Mot_Enc1.pin5, DC_Mot_Enc2.pin5
  VCC: U1.3V3, Componente1.VCC, Componente2.VCC, GY1.pin1, Grove1.VCC
  N11: U1.D18, Componente1.SDA
  N12: U1.D19, Componente1.SCL
  N13: U1.D22, Componente2.SDA, GY1.pin4, Grove1.SDA
  N14: U1.D23, Componente2.SCL, GY1.pin3, Grove1.SCL
  N15: A1.Pin_1, A1.Pin_2, S2.leg0, BAT1.+
  N16: S1.12V, S2.leg1
  N17: S1.M1-01, DC_Mot_Enc2.pin6
  N18: S1.M1-02, DC_Mot_Enc2.pin1
  N19: S1.M2-01, DC_Mot_Enc1.pin1
  N20: S1.M2-02, DC_Mot_Enc1.pin6

custom parts:
  LuaNode32 / ESP32: New Image for LuaNode32 DOIT ESP32 DEVKIT V1. Base parts from LuaNode32 / ESP32 ESP32 based LuaNode32 by G.Noorlander DOIT Esp32 DevKit v1 (30 pins long, 11 pins width) by Werner Rothschopf (modified by vanepp Dec 2018)
  Adafruit VL53L1X: The Adafruit VL53L1X Time of Flight Distance Sensor (also known as VL53L1CX) is a Time of Flight distance sensor that has a massive 4 meter range and LIDAR-like precision. The sensor contains a very tiny invisible laser source and a matching sensor. The VL53L1X can detect the "time of flight", or how long the light has taken to bounce back to the sensor. Since it uses a very narrow light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
  MPU-6050 Board GY-521: Acelerometro y Giroscopio MPU-6050 Board GY-521
  DFR0379: 20W Adjustable DC-DC Buck Converter with Digital Display.
  H-Bridge with L298N: h-bridge
  12 battery: 12V lead acid type battery, like the Husqvarna YTH2448 12V 35AH battery. This is the mini version 1/4 the size of the actual battery to be closer to typical breadboard parts (around 2in wide rathher than 7in). The pads in pcb are sized to accomidate up to 14ga wire (as these batterys will deliver high currents.)
